# Fritzing sketch final-Ayta-top-layer (saved by Fritzing 0.9.3b)
circuit board: 3.5cm x 2.5cm
circuit board: 6.5cm x 3cm
circuit board: 6.53883cm x 3.29032cm
breadboards: 1

parts:
  GY4 = double row female pin header, 40 pins [form="♀ (female)"]
  GY7 = female pin header, 4 pins [form="♀ (female)"]
  GY88 = MPU-6050 Board GY-521 [form="♀ (female)" package=THT]

nets:
  N1: GY4.pin1, GY7.pin1
  N2: GY4.pin2, GY88.pin5
  N3: GY4.pin3, GY88.pin4
  N4: GY4.pin9, GY88.pin2
  N5: GY4.pin19, GY88.pin8
  N6: GY4.pin20, GY7.pin4, GY88.pin3
  N7: GY4.pin36, GY7.pin3
  N8: GY4.pin37, GY7.pin2

custom parts:
  MPU-6050 Board GY-521: Acelerometro y Giroscopio MPU-6050 Board GY-521
