# Fritzing sketch final-ayta-bottom-layer (saved by Fritzing 0.9.3b)
circuit board: 1.7cm x 2.8cm
circuit board: 2.6cm x 3cm
circuit board: 7.07457cm x 3.57785cm
circuit board: 2.5cm x 3.5cm
circuit board: 6.5cm x 3cm
breadboards: 1

parts:
  GY4 = double row female pin header, 40 pins [form="♀ (female)"]
  GY5 = female pin header, 10 pins [form="♀ (female)"]
  Ao-VCC-GND = female pin header, 3 pins [form="♀ (female)" part_number=VCC-GND-A]
  GY6 = female pin header, 4 pins [form="♀ (female)"]
  GY7 = female pin header, 4 pins [form="♀ (female)"]  # not connected
  5v = Screw terminal - 2 pins [package=THT]

nets:
  N1: GY4.pin2, GY5.pin4
  N2: GY4.pin3, GY5.pin3
  N3: GY4.pin9, GY5.pin1, Ao-VCC-GND.pin2
  N4: GY4.pin20, GY5.pin2, Ao-VCC-GND.pin3
  N5: GY5.pin7, Ao-VCC-GND.pin1
  N6: GY6.pin1, 5v.pin1
  N7: GY6.pin2, 5v.pin2
